# Fritzing sketch 5V-3.3V Supply USB (saved by Fritzing 0.9.2b)
breadboards: 2

parts:
  U1 = mystery part, 4 pins [chip_label=NJM2396]
  C1 = Ceramic Capacitor [capacitance=100nF package="100 mil [THT, multilayer]"]
  C2 = Ceramic Capacitor [capacitance=100nF package="100 mil [THT, multilayer]"]
  C3 = Electrolytic Capacitor [capacitance=1µF package="100 mil [THT, electrolytic]"]
  C4 = Electrolytic Capacitor [capacitance=1µF package="100 mil [THT, electrolytic]"]
  U2 = mystery part, 3 pins [chip_label=TA48M033F]
  C5 = Ceramic Capacitor [capacitance=100nF package="100 mil [THT, multilayer]"]
  C6 = Ceramic Capacitor [capacitance=100nF package="100 mil [THT, multilayer]"]
  U3 = mystery part, 4 pins [chip_label="USB A"]
  R1 = Resistor [tolerance=±5% resistance=220 package=THT]
  D1 = Rectifier Diode [part_number=1N4001 package="300 mil [THT]"]
  D2 = Rectifier Diode [part_number=1N4001 package="300 mil [THT]"]
  C7 = Electrolytic Capacitor [capacitance=1µF package="100 mil [THT, electrolytic]"]

nets:
  N1: U1.pin1, C1.1, C3.+, D1.cathode
  N2: U1.pin2, C2.0, C4.+, U2.pin1, C5.1, U3.pin4, D1.anode, D2.cathode
  N3: U1.pin3, C1.0, C2.1, C3.-, C4.-, U2.pin2, C5.0, C6.0, U3.pin1, C7.-
  N4: U2.pin3, C6.1, D2.anode, C7.+
  N5: U3.pin2, R1.Pin_1
  N6: U3.pin3, R1.Pin_0

notes:
  GND
  +6V(IN)
  GND
  +5V(OUT)
  NJM2396
  1 VIN
  2 VOUT
  3 GND
  4 ON/OFF (OPEN)
  GND
  +5V(IN)
  GND
  +3.3V(OUT)
  TA48M033F
  1 VIN
  2 GND
  3 VOUT
  USB A DIP Board
  1 Vbus
  2 D-
  3 D+
  4 GND
