# Fritzing sketch TL431 Pilot Lamp (saved by Fritzing 0.9.2b)
breadboards: 2

parts:
  Power_plug1 = Power plug
  IC1 = Dual Op-Amp [package=dip08]
  U1 = mystery part, 3 pins [chip_label=TL431]
  R1 = Resistor [tolerance=±5% resistance=2.2k package=THT]
  R2 = Resistor [tolerance=±5% resistance=100k package=THT]
  R3 = Resistor [tolerance=±5% resistance=82k package=THT]
  R4 = Resistor [tolerance=±5% resistance=10k package=THT]
  LED1 = LED - 5mm [color="Red (633nm)" package="5 mm [THT]"]
  R5 = TRIMPOT [package=3362u-2]

nets:
  N1: Power_plug1.GND, IC1.A_V+, R1.Pin_0, R2.Pin_0
  N2: Power_plug1.VCC, IC1.A_V-, IC1.B_+IN, U1.pin2, LED1.cathode, R5.WIPER, R5.CW
  N3: IC1.A_OUT, R4.Pin_0
  N4: IC1.A_-IN, U1.pin1, U1.pin3, R1.Pin_1
  N5: IC1.A_+IN, R2.Pin_1, R3.Pin_0
  N6: IC1.B_-IN, IC1.B_OUT
  N7: R3.Pin_1, R5.CCW
  N8: R4.Pin_1, LED1.anode

notes:
  TL431
  REF/ANODE/CASODE
  Variable Power Supply
